# Fritzing sketch TMC2130-breakout-board (saved by Fritzing 0.9.2b)
circuit board: 5.49999cm x 2.75501cm
breadboards: 1

parts:
  E0 = male pin header, 4 pins [form="♂ (male)"]
  Z0 = male pin header, 4 pins [form="♂ (male)"]
  Y = male pin header, 4 pins [form="♂ (male)"]
  X = male pin header, 4 pins [form="♂ (male)"]
  E1 = male pin header, 4 pins [form="♂ (male)"]
  CS = male pin header, 5 pins [form="♂ (male)"]
  SC = male pin header, 3 pins [form="♂ (male)"]

nets:
  N1: E0.pin1, Z0.pin1, Y.pin1, X.pin1, E1.pin1, SC.pin1
  N2: E0.pin2, Z0.pin2, Y.pin2, X.pin2, E1.pin2, SC.pin2
  N3: E0.pin3, CS.pin4
  N4: E0.pin4, Z0.pin4, Y.pin4, X.pin4, E1.pin4, SC.pin3
  N5: Z0.pin3, CS.pin3
  N6: Y.pin3, CS.pin2
  N7: X.pin3, CS.pin1
  N8: E1.pin3, CS.pin5

notes:
  SDI
  SCK
  SDO
  CS
  E0
  Z0
  Y
  X
  -
  Z
  E1Z1
  Z1
  Breakout Board w/SPI
  M3
  For Trinamic TMC2130
  CC-BY-SA
  V 20180418
  Open Hardware
